// Digital circuit 4bit_incrementor.dig as structural Verilog
module _4bit_incrementor (
  input  [3:0] A,
  output C__out,
  output [3:0] S
);

  wire and_2_out, and_3_out, and_4_out;

  xor xor_1 (S[3], and_2_out, A[3]);
  xor xor_2 (S[2], and_3_out, A[2]);
  xor xor_3 (S[1], and_4_out, A[1]);
  xor xor_4 (S[0], 1'b1, A[0]);
  and and_1 (C__out, and_2_out, A[3]);
  and and_2 (and_2_out, and_3_out, A[2]);
  and and_3 (and_3_out, and_4_out, A[1]);
  and and_4 (and_4_out, 1'b1, A[0]);
endmodule
